# Fritzing sketch ESP8266-programmer (saved by Fritzing 0.9.4)
circuit board: 8cm x 6cm
breadboards: 1

parts:
  ESP-12F = Gizwits WiFi Witty ESP-12F
  S1 = Pushbutton [package="[THT]"]
  R2 = Resistor [tolerance=±5% resistance=10k package=THT]
  J1_ESP-01 = double row female pin header, 8 pins [form="♀ (female)"]
  J2_CH430 = double row male pin header, 8 pins [form="♂ (male)"]
  R1 = Resistor [tolerance=±5% resistance=10k package=THT]

nets:
  N1: ESP-12F.REST, S1.Pin_1, S1.Pin_2, R2.Pin_1
  N2: ESP-12F.CH_PD, ESP-12F.VCC, R2.Pin_0, J1_ESP-01.pin4, J1_ESP-01.pin6, J2_CH430.pin1
  N3: ESP-12F.GND, S1.Pin_3, S1.Pin_4, J1_ESP-01.pin8, J2_CH430.pin5, R1.Pin_1
  N4: ESP-12F.GPIO0, R1.Pin_0
  N5: ESP-12F.RXD, J1_ESP-01.pin5, J2_CH430.pin8
  N6: ESP-12F.TXD, J1_ESP-01.pin1, J2_CH430.pin4

notes:
  ESP-12F/01 Programmer Board
